# Fritzing sketch menorah (saved by Fritzing 0.9.3b)
stripboards: 2

parts:
  U1 = atmega328 [package=dip]
  Part1 = USB Mini-B Breakout [part_number=1764]
  XTAL1 = Crystal [frequency="16 Mhz" package=THT]
  C1 = Ceramic Capacitor [capacitance=100nF package="100 mil [THT, multilayer]"]
  C2 = Ceramic Capacitor [capacitance=100nF package="100 mil [THT, multilayer]"]
  S1 = Pushbutton [package="[THT]"]
  R1 = Resistor [tolerance=±5% resistance=10k package=THT]
  R2 = Resistor [tolerance=±5% resistance=220 package=THT]
  NEOPIXEL1 = Neopixel Strip -- White (60/m)

nets:
  VCC: U1.VCC, Part1.5V, NEOPIXEL1.DI
  GND: U1.GND#7, Part1.GND, C1.0, C2.0, R1.Pin_1, NEOPIXEL1.GND
  N1: U1.XLAT1, XTAL1.pin_0, C1.1
  N2: U1.XLAT2, XTAL1.pin_1, C2.1
  N3: U1.D9_(PWM), R2.Pin_1
  N4: U1.D10_(PWM), S1.Pin_3, S1.Pin_4
  N5: S1.Pin_1, S1.Pin_2, R1.Pin_0
  N6: R2.Pin_0, NEOPIXEL1.+5V

custom parts:
  USB Mini-B Breakout: Simple but effective - this breakout board has a USB Mini-B connector, with all 5 pins broken out. Great for pairing with a microcontroller with USB support, or adding USB 5V power to a project.
  Neopixel Strip -- White (60/m): Neopixel Strip, White, 60 pixels per meter.
